// Logisim project SpencerJamesPrj1372.circ as structural Verilog: 8 circuits, main circuit main
module main (
);

  wire alu_1_zero, and_1_out, clock_1_out, control_1_alusrc, control_1_branch, control_1_memwrite,
       control_1_out_6, control_1_out_7, control_1_regdst, control_1_regwrite;
  wire [1:0] control_1_aluop;
  wire [3:0] alucontrol_1_out_3;
  wire [4:0] instructionsplitter_1_out15_11, instructionsplitter_1_out20_16, instructionsplitter_1_out25_21,
       multiplexer_1_out;
  wire [5:0] instructionsplitter_1_out5_0, instructionsplitter_1_out31_26, register_1_q_2;
  wire [15:0] instructionsplitter_1_out15_0;
  wire [31:0] adder_1_out, adder_2_out, alu_1_out_5, bit_extender_1_out, datamemory_1_out_6,
       multiplexer_2_out, multiplexer_3_out, multiplexer_4_out, register_1_q, registers_1_out_7,
       registers_1_out_8, rom_1_data, shifter_1_out;

  Register #(.width(32)) register_1 (
    .D(multiplexer_3_out), .Q({register_1_q[31:8], register_1_q_2, register_1_q[1:0]}), .clk(clock_1_out));  // open: en, clr
  Clock clock_1 (.out(clock_1_out));
  Adder #(.width(32)) adder_1 (
    .a({register_1_q[31:8], register_1_q_2, register_1_q[1:0]}), .b(32'h4), .out(adder_1_out));  // open: cin, cout
  ROM #(.addrWidth(6), .dataWidth(32)) rom_1 (.addr(register_1_q_2), .data(rom_1_data));  // open: sel
  InstructionSplitter instructionsplitter_1 (
    .out5_0(instructionsplitter_1_out5_0), .out15_11(instructionsplitter_1_out15_11),
    .out20_16(instructionsplitter_1_out20_16), .out25_21(instructionsplitter_1_out25_21),
    .out31_26(instructionsplitter_1_out31_26), .out15_0(instructionsplitter_1_out15_0), .instr_in(rom_1_data));
  // Probe on instructionsplitter_1_out25_21
  Multiplexer #(.width(5)) multiplexer_1 (
    .in0(instructionsplitter_1_out20_16), .in1(instructionsplitter_1_out15_11), .out(multiplexer_1_out),
    .sel(control_1_regdst));  // open: en
  Control control_1 (
    .RegWrite(control_1_regwrite), .ALUSrc(control_1_alusrc), .MemWrite(control_1_memwrite),
    .ALUOp(control_1_aluop), .in_1(instructionsplitter_1_out31_26), .out_6(control_1_out_6),
    .out_7(control_1_out_7), .Branch(control_1_branch), .RegDst(control_1_regdst));
  assign bit_extender_1_out = {{16{instructionsplitter_1_out15_0[15]}}, instructionsplitter_1_out15_0};  // Bit_Extender bit_extender_1
  // Probe on registers_1_out_8
  Registers registers_1 (
    .Read_Reg1(instructionsplitter_1_out25_21), .Read_Reg2(instructionsplitter_1_out20_16),
    .in_4(multiplexer_4_out), .Write_Reg(multiplexer_1_out), .out_7(registers_1_out_7),
    .out_8(registers_1_out_8), .reg_write(control_1_regwrite), .clock(clock_1_out));
  Multiplexer #(.width(32)) multiplexer_2 (
    .in0(registers_1_out_8), .in1(bit_extender_1_out), .out(multiplexer_2_out), .sel(control_1_alusrc));  // open: en
  Adder #(.width(32)) adder_2 (.a(adder_1_out), .b(shifter_1_out), .out(adder_2_out));  // open: cin, cout
  Shifter #(.width(32)) shifter_1 (.in(bit_extender_1_out), .\dist (5'b00010), .out(shifter_1_out));
  ALU alu_1 (
    .in_1(registers_1_out_7), .in_2(multiplexer_2_out), .out_5(alu_1_out_5), .Zero(alu_1_zero),
    .ALU_Operation(alucontrol_1_out_3));
  ALUControl alucontrol_1 (
    .ALUOp(control_1_aluop), .Funct_Field(instructionsplitter_1_out5_0), .out_3(alucontrol_1_out_3));
  Multiplexer #(.width(32)) multiplexer_3 (
    .in0(adder_1_out), .in1(adder_2_out), .out(multiplexer_3_out), .sel(and_1_out));  // open: en
  and and_1 (and_1_out, control_1_branch, alu_1_zero);
  // Probe on registers_1_out_7
  // Probe on multiplexer_4_out
  DataMemory datamemory_1 (
    .clock(clock_1_out), .in_3(alu_1_out_5), .in_4(registers_1_out_8), .out_6(datamemory_1_out_6),
    .MemWrite(control_1_memwrite), .in_5(control_1_out_7));
  // Probe on alu_1_out_5
  // Probe on datamemory_1_out_6
  Multiplexer #(.width(32)) multiplexer_4 (
    .in0(alu_1_out_5), .in1(datamemory_1_out_6), .out(multiplexer_4_out), .sel(control_1_out_6));  // open: en

  // Notes on the sheet:
  //   PC
  //   Program Memory
  //   contents of rom_1 (hex, n*v repeats v):
  //   8c280000 8c290000 8c2a0004 148582a 11690002 1084020 1108fffc ac280008
  //   Data
  //   Memory
endmodule

module ALU (
  input  [31:0] in_1,
  input  [31:0] in_2,
  input  [3:0] ALU_Operation,
  output Zero,
  output [31:0] out_5
);

  wire subtractor_1_bout;
  wire [31:0] adder_1_out, and_1_out, multiplexer_2_out, nor_1_out, or_1_out, subtractor_1_out;

  assign and_1_out = in_1 & in_2;  // AND_Gate and_1, 32 bits wide
  assign or_1_out = in_1 | in_2;  // OR_Gate or_1, 32 bits wide
  Adder #(.width(32)) adder_1 (.a(in_1), .b(in_2), .out(adder_1_out));  // open: cin, cout
  Multiplexer #(.select(4), .width(32), .enable("false")) multiplexer_1 (
    .in0(and_1_out), .in1(or_1_out), .in2(adder_1_out), .in6(subtractor_1_out), .in7(multiplexer_2_out),
    .in12(nor_1_out), .out(out_5), .sel(ALU_Operation));  // open: in3, in4, in5, in8, in9, in10, in11, in13, in14, in15
  Subtractor #(.width(32)) subtractor_1 (
    .a(in_1), .b(in_2), .out(subtractor_1_out), .bout(subtractor_1_bout));  // open: bin
  Multiplexer #(.width(32), .enable("false")) multiplexer_2 (
    .in0({32{1'b0}}), .in1(32'h1), .out(multiplexer_2_out), .sel(subtractor_1_bout));
  Comparator #(.width(32)) comparator_1 (.a({32{1'b0}}), .b(out_5), .eq(Zero));  // open: gt, lt
  assign nor_1_out = ~(in_1 | in_2);  // NOR_Gate nor_1, 32 bits wide

  // Notes on the sheet:
  //   ALU Result
endmodule

module Registers (
  input  clock,
  input  [4:0] Read_Reg1,
  input  [4:0] Read_Reg2,
  input  [31:0] in_4,
  input  reg_write,
  input  [4:0] Write_Reg,
  output [31:0] out_7,
  output [31:0] out_8
);

  wire demultiplexer_1_out0, demultiplexer_1_out1, demultiplexer_1_out2, demultiplexer_1_out3, not_1_out,
       not_2_out, not_3_out, not_4_out, not_5_out, not_6_out, not_7_out, not_8_out, not_9_out, not_10_out,
       not_11_out, not_12_out, subtractor_1_bout, subtractor_2_bout, subtractor_3_bout, subtractor_4_bout,
       subtractor_5_bout, subtractor_6_bout, subtractor_7_bout, subtractor_8_bout, subtractor_9_bout,
       subtractor_10_bout, subtractor_11_bout, subtractor_12_bout;
  wire [1:0] priority_encoder_1_out, priority_encoder_2_out, priority_encoder_3_out;
  wire [2:0] multiplexer_1_out;
  wire [4:0] subtractor_1_out, subtractor_2_out, subtractor_3_out, subtractor_4_out, subtractor_5_out,
       subtractor_6_out, subtractor_7_out, subtractor_8_out, subtractor_9_out, subtractor_10_out,
       subtractor_11_out, subtractor_12_out;
  wire [31:0] reg8_1_out_7, reg8_1_out_8, reg8_2_out_7, reg8_2_out_8, reg8_3_out_7, reg8_3_out_8,
       reg8_4_out_7, reg8_4_out_8;

  Demultiplexer #(.select(2)) demultiplexer_1 (
    .out0(demultiplexer_1_out0), .out1(demultiplexer_1_out1), .out2(demultiplexer_1_out2),
    .out3(demultiplexer_1_out3), .in(reg_write), .sel(priority_encoder_1_out));  // open: en
  Subtractor #(.width(5)) subtractor_1 (
    .a(Write_Reg), .b({5{1'b0}}), .out(subtractor_1_out), .bout(subtractor_1_bout));  // open: bin
  Subtractor #(.width(5)) subtractor_2 (
    .a(Write_Reg), .b(5'b01000), .out(subtractor_2_out), .bout(subtractor_2_bout));  // open: bin
  Subtractor #(.width(5)) subtractor_3 (
    .a(Write_Reg), .b(5'b10000), .out(subtractor_3_out), .bout(subtractor_3_bout));  // open: bin
  Subtractor #(.width(5)) subtractor_4 (
    .a(Write_Reg), .b(5'b11000), .out(subtractor_4_out), .bout(subtractor_4_bout));  // open: bin
  Subtractor #(.width(5)) subtractor_5 (
    .a(Read_Reg1), .b({5{1'b0}}), .out(subtractor_5_out), .bout(subtractor_5_bout));  // open: bin
  Subtractor #(.width(5)) subtractor_6 (
    .a(Read_Reg1), .b(5'b01000), .out(subtractor_6_out), .bout(subtractor_6_bout));  // open: bin
  Subtractor #(.width(5)) subtractor_7 (
    .a(Read_Reg1), .b(5'b10000), .out(subtractor_7_out), .bout(subtractor_7_bout));  // open: bin
  Subtractor #(.width(5)) subtractor_8 (
    .a(Read_Reg1), .b(5'b11000), .out(subtractor_8_out), .bout(subtractor_8_bout));  // open: bin
  Subtractor #(.width(5)) subtractor_9 (
    .a(Read_Reg2), .b({5{1'b0}}), .out(subtractor_9_out), .bout(subtractor_9_bout));  // open: bin
  Subtractor #(.width(5)) subtractor_10 (
    .a(Read_Reg2), .b(5'b01000), .out(subtractor_10_out), .bout(subtractor_10_bout));  // open: bin
  Subtractor #(.width(5)) subtractor_11 (
    .a(Read_Reg2), .b(5'b10000), .out(subtractor_11_out), .bout(subtractor_11_bout));  // open: bin
  Subtractor #(.width(5)) subtractor_12 (
    .a(Read_Reg2), .b(5'b11000), .out(subtractor_12_out), .bout(subtractor_12_bout));  // open: bin
  not not_1 (not_1_out, subtractor_1_bout);
  not not_2 (not_2_out, subtractor_2_bout);
  not not_3 (not_3_out, subtractor_3_bout);
  not not_4 (not_4_out, subtractor_4_bout);
  Multiplexer #(.select(2), .width(3)) multiplexer_1 (
    .in0(subtractor_1_out[2:0]), .in1(subtractor_2_out[2:0]), .in2(subtractor_3_out[2:0]),
    .in3(subtractor_4_out[2:0]), .out(multiplexer_1_out), .sel(priority_encoder_1_out));  // open: en
  Priority_Encoder #(.select(2)) priority_encoder_1 (
    .in0(not_1_out), .in1(not_2_out), .in2(not_3_out), .in3(not_4_out), .out(priority_encoder_1_out));  // open: gs, en_out, en_in
  Reg8 reg8_1 (
    .clock(clock), .reg_1(subtractor_5_out[2:0]), .reg_2(subtractor_9_out[2:0]), .in_5(in_4),
    .write_reg(multiplexer_1_out), .out_7(reg8_1_out_7), .out_8(reg8_1_out_8),
    .reg_write__en(demultiplexer_1_out0));
  Reg8 reg8_2 (
    .clock(clock), .reg_1(subtractor_6_out[2:0]), .reg_2(subtractor_10_out[2:0]), .in_5(in_4),
    .write_reg(multiplexer_1_out), .out_7(reg8_2_out_7), .out_8(reg8_2_out_8),
    .reg_write__en(demultiplexer_1_out1));
  Reg8 reg8_3 (
    .clock(clock), .reg_1(subtractor_7_out[2:0]), .reg_2(subtractor_11_out[2:0]), .in_5(in_4),
    .write_reg(multiplexer_1_out), .out_7(reg8_3_out_7), .out_8(reg8_3_out_8),
    .reg_write__en(demultiplexer_1_out2));
  Reg8 reg8_4 (
    .clock(clock), .reg_1(subtractor_8_out[2:0]), .reg_2(subtractor_12_out[2:0]), .in_5(in_4),
    .write_reg(multiplexer_1_out), .out_7(reg8_4_out_7), .out_8(reg8_4_out_8),
    .reg_write__en(demultiplexer_1_out3));
  not not_5 (not_5_out, subtractor_5_bout);
  not not_6 (not_6_out, subtractor_6_bout);
  not not_7 (not_7_out, subtractor_7_bout);
  not not_8 (not_8_out, subtractor_8_bout);
  not not_9 (not_9_out, subtractor_9_bout);
  not not_10 (not_10_out, subtractor_10_bout);
  not not_11 (not_11_out, subtractor_11_bout);
  not not_12 (not_12_out, subtractor_12_bout);
  Priority_Encoder #(.select(2)) priority_encoder_2 (
    .in0(not_5_out), .in1(not_6_out), .in2(not_7_out), .in3(not_8_out), .out(priority_encoder_2_out));  // open: gs, en_out, en_in
  Multiplexer #(.select(2), .width(32)) multiplexer_2 (
    .in0(reg8_1_out_7), .in1(reg8_2_out_7), .in2(reg8_3_out_7), .in3(reg8_4_out_7), .out(out_7),
    .sel(priority_encoder_2_out));  // open: en
  Multiplexer #(.select(2), .width(32)) multiplexer_3 (
    .in0(reg8_1_out_8), .in1(reg8_2_out_8), .in2(reg8_3_out_8), .in3(reg8_4_out_8), .out(out_8),
    .sel(priority_encoder_3_out));  // open: en
  Priority_Encoder #(.select(2)) priority_encoder_3 (
    .in0(not_9_out), .in1(not_10_out), .in2(not_11_out), .in3(not_12_out), .out(priority_encoder_3_out));  // open: gs, en_out, en_in

  // Notes on the sheet:
  //   Write Data
  //   Read Data 1
  //   Read Data 2
endmodule

module DataMemory (
  input  MemWrite,
  input  clock,
  input  [31:0] in_3,
  input  [31:0] in_4,
  input  in_5,
  output [31:0] out_6
);

  wire [31:0] divider_1_out;

  Divider #(.width(32)) divider_1 (.a(in_3), .b(32'h4), .out(divider_1_out));  // open: upper, rem
  RAM #(.dataWidth(32), .bus("separate")) ram_1 (
    .addr(divider_1_out[7:0]), .din(in_4), .data(out_6), .str(MemWrite), .clk(clock), .ld(in_5));  // open: sel, clr

  // Notes on the sheet:
  //   address
  //   in data
  //   MemRead
  //   out data
endmodule

module Control (
  input  [5:0] in_1,
  output RegWrite,
  output ALUSrc,
  output MemWrite,
  output [1:0] ALUOp,
  output out_6,
  output out_7,
  output Branch,
  output RegDst
);

  ROM #(.addrWidth(6), .dataWidth(9)) rom_1 (
    .addr(in_1), .data({RegDst, Branch, out_7, out_6, ALUOp, MemWrite, ALUSrc, RegWrite}));  // open: sel

  // Notes on the sheet:
  //   contents of rom_1 (hex, n*v repeats v):
  //   111 111 0 0 88 30*0 63 111 111 111 4*0 6
  //   MemToReg
  //   MemRead
endmodule

module ALUControl (
  input  [1:0] ALUOp,
  input  [5:0] Funct_Field,
  output [3:0] out_3
);

  wire and_1_out, and_2_out, and_3_out, and_4_out, and_5_out, and_6_out, and_7_out, not_1_out, not_2_out,
       not_3_out, not_4_out, not_5_out, not_6_out, not_7_out, not_8_out, not_9_out, not_10_out, not_11_out,
       not_12_out, not_13_out, not_14_out, not_15_out, not_16_out, not_17_out, not_18_out, not_19_out,
       not_20_out, not_21_out, not_22_out, not_23_out, not_24_out, not_25_out, not_26_out, not_27_out,
       or_1_out, or_2_out;
  wire [2:0] priority_encoder_1_out;

  or or_1 (or_1_out, and_1_out, and_2_out);
  and and_1 (and_1_out, not_2_out, not_1_out);
  not not_1 (not_1_out, ALUOp[0]);
  not not_2 (not_2_out, ALUOp[1]);
  and and_2 (and_2_out, ALUOp[1], not_7_out, Funct_Field[5], not_3_out, not_4_out, not_5_out, not_8_out, not_6_out);
  not not_3 (not_3_out, Funct_Field[4]);
  not not_4 (not_4_out, Funct_Field[3]);
  not not_5 (not_5_out, Funct_Field[2]);
  not not_6 (not_6_out, Funct_Field[0]);
  not not_7 (not_7_out, ALUOp[0]);
  not not_8 (not_8_out, Funct_Field[1]);
  and and_3 (and_3_out, not_9_out, ALUOp[0]);
  not not_9 (not_9_out, ALUOp[1]);
  or or_2 (or_2_out, and_3_out, and_4_out);
  and and_4 (and_4_out, ALUOp[1], not_11_out, Funct_Field[5], not_10_out, not_13_out, not_12_out, Funct_Field[1], not_14_out);
  not not_10 (not_10_out, Funct_Field[4]);
  not not_11 (not_11_out, ALUOp[0]);
  not not_12 (not_12_out, Funct_Field[2]);
  not not_13 (not_13_out, Funct_Field[3]);
  and and_5 (and_5_out, ALUOp[1], not_15_out, Funct_Field[5], not_16_out, not_18_out, Funct_Field[2], not_19_out, not_20_out);
  not not_14 (not_14_out, Funct_Field[0]);
  not not_15 (not_15_out, ALUOp[0]);
  not not_16 (not_16_out, Funct_Field[4]);
  not not_17 (not_17_out, ALUOp[0]);
  not not_18 (not_18_out, Funct_Field[3]);
  not not_19 (not_19_out, Funct_Field[1]);
  not not_20 (not_20_out, Funct_Field[0]);
  and and_6 (and_6_out, ALUOp[1], not_17_out, Funct_Field[5], not_22_out, not_23_out, Funct_Field[2], not_21_out, Funct_Field[0]);
  not not_21 (not_21_out, Funct_Field[1]);
  not not_22 (not_22_out, Funct_Field[4]);
  not not_23 (not_23_out, Funct_Field[3]);
  and and_7 (and_7_out, ALUOp[1], not_24_out, Funct_Field[5], not_25_out, Funct_Field[3], not_26_out, Funct_Field[1], not_27_out);
  not not_24 (not_24_out, ALUOp[0]);
  not not_25 (not_25_out, Funct_Field[4]);
  not not_26 (not_26_out, Funct_Field[2]);
  Priority_Encoder priority_encoder_1 (
    .in0(and_5_out), .in1(and_6_out), .in2(or_1_out), .in3(or_2_out), .in4(and_7_out),
    .out(priority_encoder_1_out));  // open: in5, in6, in7, en_in, gs, en_out
  not not_27 (not_27_out, Funct_Field[0]);
  Multiplexer #(.select(3), .width(4)) multiplexer_1 (
    .in0(4'b0000), .in1(4'b0001), .in2(4'b0010), .in3(4'b0110), .in4(4'b0111), .out(out_3),
    .sel(priority_encoder_1_out));  // open: in5, in6, in7, en
endmodule

module InstructionSplitter (
  input  [31:0] instr_in,
  output [5:0] out5_0,
  output [4:0] out15_11,
  output [4:0] out20_16,
  output [4:0] out25_21,
  output [5:0] out31_26,
  output [15:0] out15_0
);


  assign out5_0 = instr_in[5:0];
  assign out15_0 = instr_in[15:0];
  assign out15_11 = instr_in[15:11];
  assign out20_16 = instr_in[20:16];
  assign out25_21 = instr_in[25:21];
  assign out31_26 = instr_in[31:26];
endmodule

module Reg8 (
  input  clock,
  input  reg_write__en,
  input  [2:0] reg_1,
  input  [2:0] reg_2,
  input  [31:0] in_5,
  input  [2:0] write_reg,
  output [31:0] out_7,
  output [31:0] out_8
);

  wire demultiplexer_1_out0, demultiplexer_1_out1, demultiplexer_1_out2, demultiplexer_1_out3,
       demultiplexer_1_out4, demultiplexer_1_out5, demultiplexer_1_out6, demultiplexer_1_out7;
  wire [31:0] register_1_q, register_2_q, register_3_q, register_4_q, register_5_q, register_6_q,
       register_7_q, register_8_q;

  Demultiplexer #(.select(3)) demultiplexer_1 (
    .out0(demultiplexer_1_out0), .out1(demultiplexer_1_out1), .out2(demultiplexer_1_out2),
    .out3(demultiplexer_1_out3), .out4(demultiplexer_1_out4), .out5(demultiplexer_1_out5),
    .out6(demultiplexer_1_out6), .out7(demultiplexer_1_out7), .in(reg_write__en), .sel(write_reg));  // open: en
  Register #(.width(32)) register_1 (.D(in_5), .en(demultiplexer_1_out0), .Q(register_1_q), .clk(clock));  // open: clr
  Register #(.width(32)) register_2 (.D(in_5), .en(demultiplexer_1_out1), .Q(register_2_q), .clk(clock));  // open: clr
  Register #(.width(32)) register_3 (.D(in_5), .en(demultiplexer_1_out2), .Q(register_3_q), .clk(clock));  // open: clr
  Register #(.width(32)) register_4 (.D(in_5), .en(demultiplexer_1_out3), .Q(register_4_q), .clk(clock));  // open: clr
  Register #(.width(32)) register_5 (.D(in_5), .en(demultiplexer_1_out4), .Q(register_5_q), .clk(clock));  // open: clr
  Register #(.width(32)) register_6 (.D(in_5), .en(demultiplexer_1_out5), .Q(register_6_q), .clk(clock));  // open: clr
  Register #(.width(32)) register_7 (.D(in_5), .en(demultiplexer_1_out6), .Q(register_7_q), .clk(clock));  // open: clr
  Register #(.width(32)) register_8 (.D(in_5), .en(demultiplexer_1_out7), .Q(register_8_q), .clk(clock));  // open: clr
  Multiplexer #(.select(3), .width(32)) multiplexer_1 (
    .in0(register_1_q), .in1(register_2_q), .in2(register_3_q), .in3(register_4_q), .in4(register_5_q),
    .in5(register_6_q), .in6(register_7_q), .in7(register_8_q), .out(out_7), .sel(reg_1));  // open: en
  Multiplexer #(.select(3), .width(32)) multiplexer_2 (
    .in0(register_1_q), .in1(register_2_q), .in2(register_3_q), .in3(register_4_q), .in4(register_5_q),
    .in5(register_6_q), .in6(register_7_q), .in7(register_8_q), .out(out_8), .sel(reg_2));  // open: en

  // Notes on the sheet:
  //   data in
endmodule
